// Logisim project 1801CS08_A2.circ as structural Verilog: 1 circuit, main circuit main
// QA
module main (
  output QA,
  output QB,
  output QC,
  output Z
);

  wire and_1_out, and_2_out, and_3_out, and_4_out, and_5_out, and_6_out, and_7_out, and_8_out, and_9_out,
       and_10_out, clock_1_out, DA, DB, DC, not_1_out, not_2_out, not_3_out, not_4_out, not_5_out, not_6_out,
       not_7_out, not_8_out, not_9_out, not_10_out, or_1_out, X, Y;

  Clock clock_1 (.out(clock_1_out));
  Shift_Register #(.length(16)) shift_register_1 (
    .in(X), .clk(clock_1_out), .out(X));  // open: shift, load, clr, d0, q0, d1, q1, d2, q2, d3, q3, d4, q4, d5, q5, d6, q6, d7, q7, d8, q8, d9, q9, d10, q10, d11, q11, d12, q12, d13, q13, d14, q14, d15, q15
  Shift_Register #(.length(16)) shift_register_2 (
    .in(Y), .clk(clock_1_out), .out(Y));  // open: shift, load, clr, d0, q0, d1, q1, d2, q2, d3, q3, d4, q4, d5, q5, d6, q6, d7, q7, d8, q8, d9, q9, d10, q10, d11, q11, d12, q12, d13, q13, d14, q14, d15, q15
  not not_1 (not_1_out, X);
  not not_2 (not_2_out, Y);
  not not_3 (not_3_out, QA);
  not not_4 (not_4_out, QB);
  and and_1 (and_1_out, QA, QB, not_1_out, not_2_out);
  and and_2 (and_2_out, X, QA, QC, not_2_out);
  and and_3 (and_3_out, not_1_out, QC, not_3_out, not_4_out);
  not not_5 (not_5_out, QC);
  or or_1 (or_1_out, not_3_out, not_4_out);
  and and_4 (and_4_out, QC, X, QA);
  not not_6 (not_6_out, QC);
  not not_7 (not_7_out, X);
  not not_8 (not_8_out, QB);
  D_Flip_Flop d_ff_1 (.clk(clock_1_out), .D(DA), .Q(QA));  // open: Qn, preset, en, reset
  and and_5 (and_5_out, QA, not_6_out, Y, not_7_out, not_8_out);
  and and_6 (and_6_out, Y, and_3_out);
  and and_7 (and_7_out, X, Y, not_5_out, not_3_out, QB);
  not not_9 (not_9_out, X);
  not not_10 (not_10_out, Y);
  and and_8 (and_8_out, not_9_out, not_10_out);
  and and_9 (and_9_out, and_4_out, Y);
  and and_10 (and_10_out, and_8_out, or_1_out);
  D_Flip_Flop d_ff_2 (.clk(clock_1_out), .D(DB), .Q(QB));  // open: Qn, preset, en, reset
  or or_2 (DB, and_4_out, and_5_out, and_7_out);
  or or_3 (DC, and_1_out, and_2_out, and_6_out);
  or or_4 (DA, and_3_out, and_9_out, and_10_out, and_7_out);
  D_Flip_Flop d_ff_3 (.clk(clock_1_out), .D(DC), .Q(QC));  // open: Qn, preset, en, reset
  and and_11 (Z, QB, QC, and_8_out);
endmodule
