// Logisim project 1801CS08_A3.circ as structural Verilog: 1 circuit, main circuit main
// DA
module main (
  output X,
  output QA,
  output QB,
  output QC,
  output DA,
  output DC,
  output DB
);

  wire and_1_out, and_2_out, and_3_out, and_4_out, and_5_out, and_6_out, and_7_out, and_8_out, clock_1_out,
       decoder_1_out0, decoder_1_out1, decoder_1_out2, decoder_1_out3, decoder_1_out4, decoder_1_out5,
       decoder_1_out6, nand_1_out, not_1_out, not_2_out, not_3_out, not_4_out, not_5_out, not_6_out,
       not_7_out;

  Shift_Register #(.length(16)) shift_register_1 (
    .in(X), .clk(clock_1_out), .out(X));  // open: shift, load, clr, d0, q0, d1, q1, d2, q2, d3, q3, d4, q4, d5, q5, d6, q6, d7, q7, d8, q8, d9, q9, d10, q10, d11, q11, d12, q12, d13, q13, d14, q14, d15, q15
  Clock clock_1 (.out(clock_1_out));
  not not_1 (not_1_out, QC);
  not not_2 (not_2_out, X);
  nand nand_1 (nand_1_out, QB, QA);
  and and_1 (and_1_out, QA, X);
  not not_3 (not_3_out, QA);
  not not_4 (not_4_out, X);
  D_Flip_Flop d_ff_1 (.clk(clock_1_out), .D(DA), .Q(QA));  // open: Qn, preset, en, reset
  and and_2 (and_2_out, nand_1_out, not_1_out, X);
  and and_3 (and_3_out, QC, not_2_out);
  not not_5 (not_5_out, and_1_out);
  or or_1 (DA, and_2_out, and_3_out);
  and and_4 (and_4_out, QC, and_1_out);
  and and_5 (and_5_out, not_5_out, QB);
  and and_6 (and_6_out, X, QC, not_3_out);
  not not_6 (not_6_out, QC);
  not not_7 (not_7_out, QB);
  and and_7 (and_7_out, QA, not_4_out);
  or or_2 (DC, and_4_out, and_5_out);
  D_Flip_Flop d_ff_2 (.clk(clock_1_out), .D(DB), .Q(QB));  // open: Qn, preset, en, reset
  and and_8 (and_8_out, not_6_out, QA, not_7_out);
  or or_3 (DB, and_6_out, and_8_out, and_7_out);
  D_Flip_Flop d_ff_3 (.clk(clock_1_out), .D(DC), .Q(QC));  // open: Qn, preset, en, reset
  Decoder #(.select(3)) decoder_1 (
    .out0(decoder_1_out0), .out1(decoder_1_out1), .out2(decoder_1_out2), .out3(decoder_1_out3),
    .out4(decoder_1_out4), .out5(decoder_1_out5), .out6(decoder_1_out6), .sel({DC, DB, DA}));  // open: out7, en
  LED R0 (.in(decoder_1_out0));
  LED R2 (.in(decoder_1_out2));
  LED R4 (.in(decoder_1_out4));
  LED R6 (.in(decoder_1_out6));
  LED R1 (.in(decoder_1_out1));
  LED R3 (.in(decoder_1_out3));
  LED R5 (.in(decoder_1_out5));
endmodule
