// Logisim project P5.circ as structural Verilog: 1 circuit, main circuit main
module main (
  input  in_1,
  input  in_2,
  input  in_3,
  input  in_4,
  output out_5
);

  wire transistor_2_out, transistor_3_out, transistor_4_out;

  Transistor #(.\type ("n")) transistor_1 (.in(1'b1), .out(out_5), .gate(in_4));
  Transistor transistor_2 (.in(1'b0), .out(transistor_2_out), .gate(in_1));
  Transistor transistor_3 (.in(transistor_2_out), .out(transistor_3_out), .gate(in_2));
  Transistor transistor_4 (.in(transistor_3_out), .out(transistor_4_out), .gate(in_3));
  Transistor transistor_5 (.in(transistor_4_out), .out(out_5), .gate(in_4));
  Transistor #(.\type ("n")) transistor_6 (.in(1'b1), .out(out_5), .gate(in_3));
  Transistor #(.\type ("n")) transistor_7 (.in(1'b1), .out(out_5), .gate(in_2));
  Transistor #(.\type ("n")) transistor_8 (.in(1'b1), .out(out_5), .gate(in_1));
endmodule
