// Logisim project L10Q1_JK.circ as structural Verilog: 1 circuit, main circuit main
module main (
  input  [1:0] in_1,
  output QA,
  output QB
);

  wire and_1_out, and_2_out, clock_1_out, not_1_out, or_1_out, xor_1_out;

  Clock clock_1 (.out(clock_1_out));
  xor xor_1 (xor_1_out, in_1[0], in_1[1]);
  J_K_Flip_Flop j_k_ff_1 (.J(xor_1_out), .clk(clock_1_out), .K(xor_1_out), .Q(QA));  // open: Qn, preset, en, reset
  not not_1 (not_1_out, QA);
  and and_1 (and_1_out, QA, in_1[0]);
  and and_2 (and_2_out, in_1[1], not_1_out);
  or or_1 (or_1_out, and_1_out, and_2_out);
  J_K_Flip_Flop j_k_ff_2 (.J(or_1_out), .clk(clock_1_out), .K(or_1_out), .Q(QB));  // open: Qn, preset, en, reset
  Hex_Digit_Display hex_digit_display_1 (.value({2'b00, QB, QA}));  // open: dp
endmodule
