// Logisim project L10Q1_SR.circ as structural Verilog: 1 circuit, main circuit main
module main (
  input  [1:0] in_1,
  output QA,
  output QB
);

  wire and_1_out, and_2_out, and_3_out, and_4_out, and_5_out, and_6_out, clock_1_out, not_1_out, not_2_out,
       not_3_out, or_1_out, xor_1_out;

  Clock clock_1 (.out(clock_1_out));
  not not_1 (not_1_out, QA);
  xor xor_1 (xor_1_out, in_1[0], in_1[1]);
  and and_1 (and_1_out, not_1_out, xor_1_out);
  and and_2 (and_2_out, QA, xor_1_out);
  S_R_Flip_Flop s_r_ff_1 (.S(and_1_out), .clk(clock_1_out), .R(and_2_out), .Q(QA));  // open: Qn, preset, reset, en
  not not_2 (not_2_out, QA);
  and and_3 (and_3_out, in_1[0], QA);
  and and_4 (and_4_out, not_2_out, in_1[1]);
  or or_1 (or_1_out, and_3_out, and_4_out);
  S_R_Flip_Flop s_r_ff_2 (.S(and_5_out), .clk(clock_1_out), .R(and_6_out), .Q(QB));  // open: Qn, preset, reset, en
  not not_3 (not_3_out, QB);
  and and_5 (and_5_out, not_3_out, or_1_out);
  and and_6 (and_6_out, or_1_out, QB);
  Hex_Digit_Display hex_digit_display_1 (.value({2'b00, QB, QA}));  // open: dp
endmodule
