// Logisim project L10Q1_T.circ as structural Verilog: 1 circuit, main circuit main
module main (
  input  [1:0] in_1,
  output QA,
  output QB
);

  wire and_1_out, and_2_out, clock_1_out, not_1_out, or_1_out, xor_1_out;

  Clock clock_1 (.out(clock_1_out));
  xor xor_1 (xor_1_out, in_1[0], in_1[1]);
  T_Flip_Flop TA (.clk(clock_1_out), .T(xor_1_out), .Q(QA));  // open: Qn, preset, reset, en
  not not_1 (not_1_out, QA);
  and and_1 (and_1_out, QA, in_1[0]);
  and and_2 (and_2_out, in_1[1], not_1_out);
  or or_1 (or_1_out, and_1_out, and_2_out);
  T_Flip_Flop TB (.clk(clock_1_out), .T(or_1_out), .Q(QB));  // open: Qn, preset, reset, en
  Hex_Digit_Display hex_digit_display_1 (.value({2'b00, QB, QA}));  // open: dp
endmodule
