// Logisim project L10Q2.circ as structural Verilog: 1 circuit, main circuit main
module main (
  input  [7:0] A,
  input  LOAD,
  input  CLEAR,
  input  [7:0] B,
  input  SHIFT_ENABLER,
  input  SHIFT_VALUE
);

  wire A_out, adder_1_cout, adder_1_out, B_out, CLOCK_out, d_ff_1_q;

  Clock CLOCK (.out(CLOCK_out));
  Shift_Register u_A (
    .shift(SHIFT_ENABLER), .in(SHIFT_VALUE), .clk(CLOCK_out), .out(A_out), .load(LOAD), .clr(CLEAR),
    .d0(A[7]), .d1(A[6]), .d2(A[5]), .d3(A[4]), .d4(A[3]), .d5(A[2]), .d6(A[1]), .d7(A[0]));  // open: q0, q1, q2, q3, q4, q5, q6, q7
  Shift_Register u_B (
    .shift(SHIFT_ENABLER), .in(SHIFT_VALUE), .clk(CLOCK_out), .out(B_out), .load(LOAD), .clr(CLEAR),
    .d0(B[7]), .d1(B[6]), .d2(B[5]), .d3(B[4]), .d4(B[3]), .d5(B[2]), .d6(B[1]), .d7(B[0]));  // open: q0, q1, q2, q3, q4, q5, q6, q7
  Adder #(.width(1)) adder_1 (.a(A_out), .b(B_out), .out(adder_1_out), .cin(d_ff_1_q), .cout(adder_1_cout));
  D_Flip_Flop d_ff_1 (.clk(CLOCK_out), .D(adder_1_cout), .Q(d_ff_1_q));  // open: Qn, preset, en, reset
  Shift_Register SUM (
    .shift(SHIFT_ENABLER), .in(adder_1_out), .clk(CLOCK_out), .clr(CLEAR));  // open: out, load, d0, q0, d1, q1, d2, q2, d3, q3, d4, q4, d5, q5, d6, q6, d7, q7
endmodule
