// Logisim project L10Q3.circ as structural Verilog: 2 circuits, main circuit main
module main (
);

  wire clock_1_out, nor_1_out;
  wire [3:0] n2_bit_aschynchronous_2_qa;

  _2_Bit_Aschynchronous u_2_bit_aschynchronous_1 (
    .CLOCK(nor_1_out), .QA(n2_bit_aschynchronous_2_qa[2]), .QB(n2_bit_aschynchronous_2_qa[3]));
  nor nor_1 (nor_1_out, n2_bit_aschynchronous_2_qa[0], n2_bit_aschynchronous_2_qa[1]);
  Clock clock_1 (.out(clock_1_out));
  _2_Bit_Aschynchronous u_2_bit_aschynchronous_2 (
    .CLOCK(clock_1_out), .QA(n2_bit_aschynchronous_2_qa[0]), .QB(n2_bit_aschynchronous_2_qa[1]));
  Hex_Digit_Display hex_digit_display_1 (.value(n2_bit_aschynchronous_2_qa));  // open: dp
endmodule

module _2_Bit_Aschynchronous (
  input  CLOCK,
  output QA,
  output QB
);

  T_Flip_Flop TA (.clk(CLOCK), .T(1'b1), .Q(QA));  // open: Qn, preset, reset, en
  T_Flip_Flop TB (.clk(CLOCK), .T(QA), .Q(QB));  // open: Qn, preset, reset, en
endmodule
