// Logisim project L11Q2_JK-moore.circ as structural Verilog: 1 circuit, main circuit main
module main (
  output INPUT_X,
  output QA,
  output QB,
  output QC,
  output Y
);

  wire and_3_out, and_4_out, BCX, clock_1_out, JB, JC, not_1_out, not_2_out, not_3_out, or_1_out;

  Shift_Register #(.length(16)) shift_register_1 (
    .shift(1'b1), .in(INPUT_X), .clk(clock_1_out), .out(INPUT_X));  // open: load, clr, d0, q0, d1, q1, d2, q2, d3, q3, d4, q4, d5, q5, d6, q6, d7, q7, d8, q8, d9, q9, d10, q10, d11, q11, d12, q12, d13, q13, d14, q14, d15, q15
  Clock clock_1 (.out(clock_1_out));
  not not_1 (not_1_out, INPUT_X);
  and and_1 (BCX, QB, QC, INPUT_X);
  or or_1 (or_1_out, QC, QA);
  not not_2 (not_2_out, QA);
  not not_3 (not_3_out, QB);
  and and_2 (JB, INPUT_X, or_1_out);
  and and_3 (and_3_out, not_2_out, INPUT_X, not_3_out);
  and and_4 (and_4_out, QB, not_1_out);
  J_K_Flip_Flop j_k_ff_1 (.J(BCX), .clk(clock_1_out), .K(1'b1), .Q(QA));  // open: Qn, preset, en, reset
  or or_2 (JC, and_3_out, and_4_out);
  J_K_Flip_Flop j_k_ff_2 (.J(JB), .clk(clock_1_out), .K(QC), .Q(QB));  // open: Qn, preset, en, reset
  J_K_Flip_Flop j_k_ff_3 (.J(JC), .clk(clock_1_out), .K(1'b1), .Q(QC));  // open: Qn, preset, en, reset

  assign Y = QA;

  // Other names for the same wires on the sheet: X = INPUT_X
endmodule
