// Logisim project L11Q2_T-mealy.circ as structural Verilog: 1 circuit, main circuit main
module main (
  output QB,
  output INPUT_X,
  output QA,
  output Y
);

  wire A_B, B_X, BXC, clock_1_out, not_1_out, or_1_out, or_2_out, xor_1_out;

  Clock clock_1 (.out(clock_1_out));
  Shift_Register #(.length(16)) shift_register_1 (
    .shift(1'b1), .in(INPUT_X), .clk(clock_1_out), .out(INPUT_X));  // open: load, clr, d0, q0, d1, q1, d2, q2, d3, q3, d4, q4, d5, q5, d6, q6, d7, q7, d8, q8, d9, q9, d10, q10, d11, q11, d12, q12, d13, q13, d14, q14, d15, q15
  or or_1 (or_1_out, B_X, A_B);
  T_Flip_Flop A (.clk(clock_1_out), .T(or_1_out), .Q(QA));  // open: Qn, preset, reset, en
  not not_1 (not_1_out, INPUT_X);
  xor xor_1 (xor_1_out, INPUT_X, QA);
  or or_2 (or_2_out, BXC, xor_1_out);
  T_Flip_Flop B (.clk(clock_1_out), .T(or_2_out), .Q(QB));  // open: Qn, preset, reset, en
  and and_1 (A_B, QB, QA);
  and and_2 (BXC, not_1_out, QB);
  and and_3 (B_X, QB, INPUT_X);
  and and_4 (Y, INPUT_X, A_B);

  // Other names for the same wires on the sheet: X = INPUT_X
endmodule
