// Logisim project L11Q2_T-moore.circ as structural Verilog: 1 circuit, main circuit main
module main (
  output QA,
  output QB,
  output QC,
  output Y,
  output INPUT_X
);

  wire and_1_out, and_2_out, and_3_out, and_4_out, B_C, clock_1_out, not_1_out, not_2_out, not_3_out,
       or_1_out, or_2_out, TB, TC;

  Clock clock_1 (.out(clock_1_out));
  or or_1 (or_1_out, QA, and_1_out);
  and and_1 (and_1_out, B_C, INPUT_X);
  T_Flip_Flop t_ff_1 (.clk(clock_1_out), .T(or_1_out), .Q(QA));  // open: Qn, preset, reset, en
  and and_2 (and_2_out, INPUT_X, or_2_out);
  or or_2 (or_2_out, QA, QC);
  not not_1 (not_1_out, QA);
  not not_2 (not_2_out, QB);
  not not_3 (not_3_out, INPUT_X);
  and and_3 (and_3_out, INPUT_X, not_1_out, not_2_out);
  and and_4 (and_4_out, QB, not_3_out);
  T_Flip_Flop t_ff_2 (.clk(clock_1_out), .T(TB), .Q(QB));  // open: Qn, preset, reset, en
  or or_3 (TB, B_C, and_2_out);
  or or_4 (TC, QC, and_4_out, and_3_out);
  T_Flip_Flop t_ff_3 (.clk(clock_1_out), .T(TC), .Q(QC));  // open: Qn, preset, reset, en
  Shift_Register #(.length(16)) SEQUENCE (
    .shift(1'b1), .in(INPUT_X), .clk(clock_1_out), .out(INPUT_X));  // open: load, clr, d0, q0, d1, q1, d2, q2, d3, q3, d4, q4, d5, q5, d6, q6, d7, q7, d8, q8, d9, q9, d10, q10, d11, q11, d12, q12, d13, q13, d14, q14, d15, q15
  and and_5 (B_C, QC, QB);

  assign Y = QA;

  // Other names for the same wires on the sheet: X = INPUT_X
endmodule
