// Logisim project L11Q3.circ as structural Verilog: 1 circuit, main circuit main
module main (
  input  [7:0] A,
  input  LOAD,
  input  SHIFT_ENABLER,
  input  [7:0] B,
  input  [7:0] C,
  input  [7:0] D,
  input  SHIFT_VALUE,
  input  CLEAR,
  output [7:0] AVERAGE
);

  wire A_out, adder_1_cout, adder_1_out, B_out, C_out, clock_1_out, d_ff_1_q, D_out;

  Clock clock_1 (.out(clock_1_out));
  Shift_Register u_A (
    .shift(SHIFT_ENABLER), .in(adder_1_out), .clk(clock_1_out), .out(A_out), .load(LOAD), .clr(CLEAR),
    .d0(A[7]), .d1(A[6]), .d2(A[5]), .d3(A[4]), .d4(A[3]), .d5(A[2]), .d6(A[1]), .d7(A[0]));  // open: q0, q1, q2, q3, q4, q5, q6, q7
  Shift_Register u_B (
    .shift(SHIFT_ENABLER), .in(C_out), .clk(clock_1_out), .out(B_out), .load(LOAD), .clr(CLEAR), .d0(B[7]),
    .d1(B[6]), .d2(B[5]), .d3(B[4]), .d4(B[3]), .d5(B[2]), .d6(B[1]), .d7(B[0]));  // open: q0, q1, q2, q3, q4, q5, q6, q7
  Shift_Register u_C (
    .shift(SHIFT_ENABLER), .in(D_out), .clk(clock_1_out), .out(C_out), .load(LOAD), .clr(CLEAR), .d0(C[7]),
    .d1(C[6]), .d2(C[5]), .d3(C[4]), .d4(C[3]), .d5(C[2]), .d6(C[1]), .d7(C[0]));  // open: q0, q1, q2, q3, q4, q5, q6, q7
  Shift_Register u_D (
    .shift(SHIFT_ENABLER), .in(SHIFT_VALUE), .clk(clock_1_out), .out(D_out), .load(LOAD), .clr(CLEAR),
    .d0(D[7]), .d1(D[6]), .d2(D[5]), .d3(D[4]), .d4(D[3]), .d5(D[2]), .d6(D[1]), .d7(D[0]));  // open: q0, q1, q2, q3, q4, q5, q6, q7
  Adder #(.width(1)) adder_1 (.a(A_out), .b(B_out), .out(adder_1_out), .cin(d_ff_1_q), .cout(adder_1_cout));
  Shift_Register OUTPUT (
    .shift(SHIFT_ENABLER), .in(adder_1_out), .clk(clock_1_out), .clr(CLEAR), .q0(AVERAGE[7]),
    .q1(AVERAGE[6]), .q2(AVERAGE[5]), .q3(AVERAGE[4]), .q4(AVERAGE[3]), .q5(AVERAGE[2]), .q6(AVERAGE[1]),
    .q7(AVERAGE[0]));  // open: out, load, d0, d1, d2, d3, d4, d5, d6, d7
  D_Flip_Flop d_ff_1 (.clk(clock_1_out), .D(adder_1_cout), .Q(d_ff_1_q));  // open: Qn, preset, en, reset
endmodule
