// Logisim project LAB14_Q3C.circ as structural Verilog: 2 circuits, main circuit main
module main (
  input  [7:0] DATA_INPUT,
  input  [2:0] in_2,
  input  [7:0] C0,
  output [2:0] out_4,
  output ZEROFLAG,
  output [7:0] OUTPUT
);

  wire clock_1_out, decoder_1_out1, decoder_1_out2, decoder_1_out3, decoder_1_out4, decoder_1_out5,
       decoder_1_out6, decoder_1_out7;
  wire [1:0] CUR, NEXT;
  wire [2:0] SELA, SELB;
  wire [7:0] multiplexer_1_out, multiplexer_2_out, register_1_q, register_2_q, register_3_q, register_4_q,
       register_5_q, register_6_q, register_7_q;

  Clock clock_1 (.out(clock_1_out));
  Decoder #(.select(3)) decoder_1 (
    .out1(decoder_1_out1), .out2(decoder_1_out2), .out3(decoder_1_out3), .out4(decoder_1_out4),
    .out5(decoder_1_out5), .out6(decoder_1_out6), .out7(decoder_1_out7), .sel(out_4));  // open: out0, en
  Register register_1 (.D(OUTPUT), .en(decoder_1_out1), .Q(register_1_q), .clk(clock_1_out));  // open: clr
  Register register_2 (.D(OUTPUT), .en(decoder_1_out2), .Q(register_2_q), .clk(clock_1_out));  // open: clr
  Register register_3 (.en(decoder_1_out3), .Q(register_3_q), .clk(clock_1_out));  // open: D, clr
  Register register_4 (.D(OUTPUT), .en(decoder_1_out4), .Q(register_4_q), .clk(clock_1_out));  // open: clr
  Register register_5 (.D(OUTPUT), .en(decoder_1_out5), .Q(register_5_q), .clk(clock_1_out));  // open: clr
  Register register_6 (.D(OUTPUT), .en(decoder_1_out6), .Q(register_6_q), .clk(clock_1_out));  // open: clr
  Register register_7 (.D(OUTPUT), .en(decoder_1_out7), .Q(register_7_q), .clk(clock_1_out));  // open: clr
  Multiplexer #(.select(3), .width(8)) multiplexer_1 (
    .in0(DATA_INPUT), .in1(register_1_q), .in2(register_2_q), .in3(register_3_q), .in4(register_4_q),
    .in5(register_5_q), .in6(register_6_q), .in7(register_7_q), .out(multiplexer_1_out), .sel(SELA));  // open: en
  Multiplexer #(.select(3), .width(8)) multiplexer_2 (
    .in0(DATA_INPUT), .in1(register_1_q), .in2(register_2_q), .in3(register_3_q), .in4(register_4_q),
    .in5(register_5_q), .in6(register_6_q), .in7(register_7_q), .out(multiplexer_2_out), .sel(SELB));  // open: en
  Register #(.width(2)) register_8 (.D(NEXT), .Q(CUR), .clk(clock_1_out));  // open: en, clr
  Multiplexer #(.select(2), .width(2)) multiplexer_3 (
    .in0(2'b01), .in1(2'b10), .in2(2'b00), .in3(2'b00), .out(NEXT), .sel(CUR));  // open: en
  ALU_16 alu_16_1 (
    .A(multiplexer_1_out), .B(multiplexer_2_out), .C0(C0), .SELECTOR(in_2), .ZEROFLAG(ZEROFLAG),
    .OUTPUT(OUTPUT));  // open: in_4
  Multiplexer #(.select(2), .width(3)) multiplexer_4 (
    .in0(3'b001), .in1(3'b010), .in2(3'b111), .in3(3'b000), .out(out_4), .sel(CUR));  // open: en
  Multiplexer #(.select(2), .width(3)) multiplexer_5 (
    .in0(3'b100), .in1(3'b000), .in2(3'b010), .in3(3'b000), .out(SELA), .sel(CUR));  // open: en
  Multiplexer #(.select(2), .width(3)) multiplexer_6 (
    .in0(3'b000), .in1(3'b100), .in2(3'b001), .in3(3'b000), .out(SELB), .sel(CUR));  // open: en

  // Other names for the same wires on the sheet: SELD[2:0] = out_4
endmodule

// ALU
module ALU_16 (
  input  [7:0] A,
  input  [7:0] B,
  input  [7:0] C0,
  input  in_4,
  input  [2:0] SELECTOR,
  output ZEROFLAG,
  output [7:0] OUTPUT
);

  wire [7:0] adder_1_out, and_1_out, divider_1_out, multiplier_1_out, or_1_out, subtractor_1_out, xor_1_out;

  Adder adder_1 (.a(A), .b(B), .out(adder_1_out), .cin(in_4));  // open: cout
  Subtractor subtractor_1 (.a(A), .b(B), .out(subtractor_1_out), .bin(in_4));  // open: bout
  Multiplier multiplier_1 (.a(A), .b(B), .out(multiplier_1_out), .cin(C0));  // open: cout
  Divider divider_1 (.a(A), .b(B), .out(divider_1_out), .upper(C0));  // open: rem
  assign and_1_out = A & B;  // AND_Gate and_1, 8 bits wide
  assign or_1_out = A | B;  // OR_Gate or_1, 8 bits wide
  assign xor_1_out = A ^ B;  // XOR_Gate xor_1, 8 bits wide
  Multiplexer #(.select(3), .width(8)) multiplexer_1 (
    .in0(adder_1_out), .in1(subtractor_1_out), .in2(multiplier_1_out), .in3(divider_1_out), .in4(and_1_out),
    .in5(or_1_out), .in6(xor_1_out), .in7(A), .out(OUTPUT), .sel(SELECTOR));  // open: en
  Comparator comparator_1 (.a(OUTPUT), .b(C0), .eq(ZEROFLAG));  // open: gt, lt
endmodule
