// Logisim project p1.circ as structural Verilog: 1 circuit, main circuit main
module main (
  input  in_1,
  input  in_2,
  input  in_3,
  input  in_4,
  input  in_5,
  input  in_6,
  input  in_7,
  input  in_8,
  output out_9,
  output out_10
);

  wire transistor_1_out, transistor_2_out, transistor_3_out, transistor_4_out, transistor_5_out,
       transistor_6_out;

  Transistor transistor_1 (.in(1'b1), .out(transistor_1_out), .gate(in_1));
  Transistor #(.\type ("n")) transistor_2 (.in(1'b1), .out(transistor_2_out), .gate(in_5));
  Transistor transistor_3 (.in(transistor_1_out), .out(transistor_3_out), .gate(in_2));
  Transistor #(.\type ("n")) transistor_4 (.in(transistor_2_out), .out(transistor_4_out), .gate(in_6));
  Transistor #(.\type ("n")) transistor_5 (.in(transistor_4_out), .out(transistor_5_out), .gate(in_7));
  Transistor transistor_6 (.in(transistor_3_out), .out(transistor_6_out), .gate(in_3));
  Transistor transistor_7 (.in(transistor_6_out), .out(out_9), .gate(in_4));
  Transistor #(.\type ("n")) transistor_8 (.in(transistor_5_out), .out(out_10), .gate(in_8));
endmodule
