// Logisim project p2.circ as structural Verilog: 1 circuit, main circuit main
module main (
  input  in_1,
  input  in_2,
  input  C,
  input  D,
  input  E,
  output out_6,
  output out_7,
  output out_8,
  output out_9
);

  wire transistor_2_out, transistor_3_out, transistor_4_out, transistor_5_out, transistor_7_out,
       transistor_8_out, transistor_9_out, transistor_10_out;

  Pull_Resistor #(.pull(1)) pull_resistor_1 (.node(out_7));
  Transistor #(.\type ("n")) transistor_1 (.in(transistor_2_out), .out(out_7), .gate(in_1));
  Transistor #(.\type ("n")) transistor_2 (.in(transistor_3_out), .out(transistor_2_out), .gate(in_2));
  Transistor #(.\type ("n")) transistor_3 (.in(transistor_4_out), .out(transistor_3_out), .gate(C));
  Transistor #(.\type ("n")) transistor_4 (.in(transistor_5_out), .out(transistor_4_out), .gate(D));
  Transistor #(.\type ("n")) transistor_5 (.in(1'b0), .out(transistor_5_out), .gate(E));
  Pull_Resistor pull_resistor_2 (.node(out_8));
  Transistor #(.\type ("n")) transistor_6 (.in(transistor_7_out), .out(out_8), .gate(in_1));
  Transistor #(.\type ("n")) transistor_7 (.in(transistor_8_out), .out(transistor_7_out), .gate(in_2));
  Transistor #(.\type ("n")) transistor_8 (.in(transistor_9_out), .out(transistor_8_out), .gate(C));
  Transistor #(.\type ("n")) transistor_9 (.in(transistor_10_out), .out(transistor_9_out), .gate(D));
  Transistor #(.\type ("n")) transistor_10 (.in(1'b1), .out(transistor_10_out), .gate(E));
  Transistor #(.\type ("n")) transistor_11 (.in(1'b0), .out(out_6), .gate(in_1));
  Transistor #(.\type ("n")) transistor_12 (.in(1'b1), .out(out_9), .gate(in_1));
  Transistor #(.\type ("n")) transistor_13 (.in(1'b0), .out(out_6), .gate(in_2));
  Transistor #(.\type ("n")) transistor_14 (.in(1'b1), .out(out_9), .gate(in_2));
  Pull_Resistor #(.pull(1)) pull_resistor_3 (.node(out_6));
  Transistor #(.\type ("n")) transistor_15 (.in(1'b0), .out(out_6), .gate(C));
  Pull_Resistor pull_resistor_4 (.node(out_9));
  Transistor #(.\type ("n")) transistor_16 (.in(1'b1), .out(out_9), .gate(C));
  Transistor #(.\type ("n")) transistor_17 (.in(1'b0), .out(out_6), .gate(D));
  Transistor #(.\type ("n")) transistor_18 (.in(1'b1), .out(out_9), .gate(D));
  Transistor #(.\type ("n")) transistor_19 (.in(1'b0), .out(out_6), .gate(E));
  Transistor #(.\type ("n")) transistor_20 (.in(1'b1), .out(out_9), .gate(E));

  // Other names for the same wires on the sheet: A = in_1; B = in_2
endmodule
