// Logisim project p3.circ as structural Verilog: 1 circuit, main circuit main
module main (
  input  in_1,
  input  in_2,
  input  in_3,
  input  in_4,
  input  in_5,
  output out_6
);

  wire transistor_2_out, transistor_3_out, transistor_4_out, transistor_7_out;

  Transistor #(.\type ("n")) transistor_1 (.in(transistor_2_out), .out(out_6), .gate(in_1));
  Transistor #(.\type ("n")) transistor_2 (.in(1'b0), .out(transistor_2_out), .gate(in_4));
  Transistor transistor_3 (.in(1'b1), .out(transistor_3_out), .gate(in_3));
  Transistor transistor_4 (.in(transistor_3_out), .out(transistor_4_out), .gate(in_2));
  Transistor transistor_5 (.in(transistor_4_out), .out(out_6), .gate(in_1));
  Transistor #(.\type ("n")) transistor_6 (.in(transistor_7_out), .out(out_6), .gate(in_2));
  Transistor #(.\type ("n")) transistor_7 (.in(1'b0), .out(transistor_7_out), .gate(in_5));
  Transistor transistor_8 (.in(transistor_3_out), .out(transistor_4_out), .gate(in_5));
  Transistor transistor_9 (.in(transistor_4_out), .out(out_6), .gate(in_4));
  Transistor #(.\type ("n")) transistor_10 (.in(1'b0), .out(out_6), .gate(in_3));

  // Other names for the same wires on the sheet: A = in_1; B = in_4; C = in_2; D = in_5; E = in_3
endmodule
