// Logisim project p6.circ as structural Verilog: 5 circuits, main circuit main
module main (
  input  A,
  input  B,
  input  D,
  input  C,
  output out_5
);

  wire and_1_out_3;

  AND and_1 (.in_1(B), .in_2(C), .out_3(and_1_out_3));
  OR4 or4_1 (.in_1(A), .in_2(and_1_out_3), .in_3(and_1_out_3), .in_4(D), .out_5(out_5));
endmodule

module NAND2 (
  input  in_1,
  input  in_2,
  output out_3
);

  wire transistor_4_out;

  Transistor transistor_1 (.in(1'b1), .out(out_3), .gate(in_1));
  Transistor transistor_2 (.in(1'b1), .out(out_3), .gate(in_2));
  Transistor #(.\type ("n")) transistor_3 (.in(transistor_4_out), .out(out_3), .gate(in_1));
  Transistor #(.\type ("n")) transistor_4 (.in(1'b0), .out(transistor_4_out), .gate(in_2));
endmodule

module NOR (
  input  in_1,
  input  in_2,
  output out_3
);

  wire transistor_3_out;

  Transistor #(.\type ("n")) transistor_1 (.in(1'b0), .out(out_3), .gate(in_1));
  Transistor transistor_2 (.in(transistor_3_out), .out(out_3), .gate(in_1));
  Transistor transistor_3 (.in(1'b1), .out(transistor_3_out), .gate(in_2));
  Transistor #(.\type ("n")) transistor_4 (.in(1'b0), .out(out_3), .gate(in_2));
endmodule

module AND (
  input  in_1,
  input  in_2,
  output out_3
);

  wire transistor_3_out;

  Transistor transistor_1 (.in(1'b0), .out(out_3), .gate(in_1));
  Transistor #(.\type ("n")) transistor_2 (.in(transistor_3_out), .out(out_3), .gate(in_1));
  Transistor #(.\type ("n")) transistor_3 (.in(1'b1), .out(transistor_3_out), .gate(in_2));
  Transistor transistor_4 (.in(1'b0), .out(out_3), .gate(in_2));
endmodule

module OR4 (
  input  in_1,
  input  in_2,
  input  in_3,
  input  in_4,
  output out_5
);

  wire transistor_2_out, transistor_3_out, transistor_4_out;

  Transistor #(.\type ("n")) transistor_1 (.in(1'b1), .out(out_5), .gate(in_4));
  Transistor transistor_2 (.in(1'b0), .out(transistor_2_out), .gate(in_1));
  Transistor transistor_3 (.in(transistor_2_out), .out(transistor_3_out), .gate(in_2));
  Transistor transistor_4 (.in(transistor_3_out), .out(transistor_4_out), .gate(in_3));
  Transistor transistor_5 (.in(transistor_4_out), .out(out_5), .gate(in_4));
  Transistor #(.\type ("n")) transistor_6 (.in(1'b1), .out(out_5), .gate(in_3));
  Transistor #(.\type ("n")) transistor_7 (.in(1'b1), .out(out_5), .gate(in_2));
  Transistor #(.\type ("n")) transistor_8 (.in(1'b1), .out(out_5), .gate(in_1));
endmodule
