// Logisim project p7.circ as structural Verilog: 1 circuit, main circuit main
module main (
  input  in_1,
  input  in_2,
  input  in_3,
  input  in_4,
  input  in_5,
  input  in_6,
  output out_7,
  output out_8,
  output out_9
);

  wire transistor_7_out, transistor_8_out, transistor_9_out, transistor_10_out, transistor_11_out,
       transistor_19_out, transistor_20_out, transistor_21_out, transistor_22_out, transistor_23_out,
       transistor_29_out, transistor_30_out, transistor_31_out, transistor_32_out, transistor_33_out;

  Transistor transistor_1 (.in(1'b1), .out(out_8), .gate(in_1));
  Transistor transistor_2 (.in(1'b1), .out(out_8), .gate(in_3));
  Transistor transistor_3 (.in(1'b1), .out(out_8), .gate(in_2));
  Transistor transistor_4 (.in(1'b1), .out(out_8), .gate(in_5));
  Transistor transistor_5 (.in(1'b1), .out(out_8), .gate(in_4));
  Transistor #(.\type ("n")) transistor_6 (.in(transistor_7_out), .out(out_8), .gate(in_1));
  Transistor #(.\type ("n")) transistor_7 (.in(transistor_8_out), .out(transistor_7_out), .gate(in_2));
  Transistor #(.\type ("n")) transistor_8 (.in(transistor_9_out), .out(transistor_8_out), .gate(in_3));
  Transistor #(.\type ("n")) transistor_9 (.in(transistor_10_out), .out(transistor_9_out), .gate(in_4));
  Transistor #(.\type ("n")) transistor_10 (.in(transistor_11_out), .out(transistor_10_out), .gate(in_5));
  Transistor #(.\type ("n")) transistor_11 (.in(1'b0), .out(transistor_11_out), .gate(in_6));
  Transistor transistor_12 (.in(1'b1), .out(out_8), .gate(in_6));
  Transistor transistor_13 (.in(1'b0), .out(out_9), .gate(in_1));
  Transistor transistor_14 (.in(1'b0), .out(out_9), .gate(in_3));
  Transistor transistor_15 (.in(1'b0), .out(out_9), .gate(in_2));
  Transistor transistor_16 (.in(1'b0), .out(out_9), .gate(in_5));
  Transistor transistor_17 (.in(1'b0), .out(out_9), .gate(in_4));
  Transistor #(.\type ("n")) transistor_18 (.in(transistor_19_out), .out(out_9), .gate(in_1));
  Transistor #(.\type ("n")) transistor_19 (.in(transistor_20_out), .out(transistor_19_out), .gate(in_2));
  Transistor #(.\type ("n")) transistor_20 (.in(transistor_21_out), .out(transistor_20_out), .gate(in_3));
  Transistor #(.\type ("n")) transistor_21 (.in(transistor_22_out), .out(transistor_21_out), .gate(in_4));
  Transistor #(.\type ("n")) transistor_22 (.in(transistor_23_out), .out(transistor_22_out), .gate(in_5));
  Transistor #(.\type ("n")) transistor_23 (.in(1'b1), .out(transistor_23_out), .gate(in_6));
  Transistor transistor_24 (.in(1'b0), .out(out_9), .gate(in_6));
  Transistor #(.\type ("n")) transistor_25 (.in(1'b0), .out(out_7), .gate(in_1));
  Transistor #(.\type ("n")) transistor_26 (.in(1'b0), .out(out_7), .gate(in_3));
  Transistor #(.\type ("n")) transistor_27 (.in(1'b0), .out(out_7), .gate(in_2));
  Transistor transistor_28 (.in(transistor_29_out), .out(out_7), .gate(in_1));
  Transistor transistor_29 (.in(transistor_30_out), .out(transistor_29_out), .gate(in_2));
  Transistor transistor_30 (.in(transistor_31_out), .out(transistor_30_out), .gate(in_3));
  Transistor transistor_31 (.in(transistor_32_out), .out(transistor_31_out), .gate(in_4));
  Transistor transistor_32 (.in(transistor_33_out), .out(transistor_32_out), .gate(in_5));
  Transistor transistor_33 (.in(1'b1), .out(transistor_33_out), .gate(in_6));
  Transistor #(.\type ("n")) transistor_34 (.in(1'b0), .out(out_7), .gate(in_4));
  Transistor #(.\type ("n")) transistor_35 (.in(1'b0), .out(out_7), .gate(in_5));
  Transistor #(.\type ("n")) transistor_36 (.in(1'b0), .out(out_7), .gate(in_6));

  // Other names for the same wires on the sheet: A = in_1; B = in_2; C = in_3; D = in_4; E = in_5; F = in_6

  // Notes on the sheet:
  //   NAND
  //   AND
  //   NOR
endmodule
