// Logisim project p10.circ as structural Verilog: 1 circuit, main circuit main
module main (
  input  a0,
  input  b0,
  input  a1,
  input  b1,
  output s0,
  output s1,
  output s2
);

  wire and_1_out, and_2_out, and_3_out, xor_2_out;

  xor xor_1 (s0, a0, b0);
  and and_1 (and_1_out, b0, a0);
  xor xor_2 (xor_2_out, and_1_out, a1);
  xor xor_3 (s1, xor_2_out, b1);
  and and_2 (and_2_out, xor_2_out, b1);
  and and_3 (and_3_out, and_1_out, a1);
  or or_1 (s2, and_2_out, and_3_out);
endmodule
