// Logisim project p4.circ as structural Verilog: 1 circuit, main circuit main
module main (
  input  A,
  input  B,
  input  C,
  input  D,
  input  s2,
  input  s3,
  input  s1,
  output out_8
);

  wire and_1_out, and_2_out, and_3_out, and_4_out, not_1_out, not_2_out, or_1_out, or_2_out;

  or or_1 (or_1_out, s2, s3);
  or or_2 (or_2_out, s3, s1);
  not not_1 (not_1_out, or_1_out);
  not not_2 (not_2_out, or_2_out);
  and and_1 (and_1_out, A, not_1_out, not_2_out);
  and and_2 (and_2_out, B, not_1_out, or_2_out);
  and and_3 (and_3_out, C, or_1_out, not_2_out);
  and and_4 (and_4_out, D, or_1_out, or_2_out);
  or or_3 (out_8, and_1_out, and_2_out, and_3_out, and_4_out);

  // Notes on the sheet:
  //   BLOCK A
  //   BLOCK B
endmodule
