// Logisim project p5.circ as structural Verilog: 2 circuits, main circuit main
module main (
  input  a3,
  input  b3,
  input  a2,
  input  b2,
  input  a1,
  input  b1,
  input  a0,
  input  b0,
  input  in_9,
  output c3,
  output c2,
  output c1,
  output c0
);

  Multiplexer multiplexer_1 (.i0(a3), .i1(b3), .s0(in_9), .out_4(c3));
  Multiplexer multiplexer_2 (.i0(a2), .i1(b2), .s0(in_9), .out_4(c2));
  Multiplexer multiplexer_3 (.i0(a1), .i1(b1), .s0(in_9), .out_4(c1));
  Multiplexer multiplexer_4 (.i0(a0), .i1(b0), .s0(in_9), .out_4(c0));
endmodule

module Multiplexer (
  input  i0,
  input  i1,
  input  s0,
  output out_4
);

  wire and_1_out, and_2_out, not_1_out;

  not not_1 (not_1_out, s0);
  and and_1 (and_1_out, i0, not_1_out);
  and and_2 (and_2_out, i1, s0);
  or or_1 (out_4, and_1_out, and_2_out);
endmodule
