// Logisim project p6.circ as structural Verilog: 2 circuits, main circuit main
module main (
  input  a3,
  input  b3,
  input  c3,
  input  d3,
  input  a2,
  input  b2,
  input  c2,
  input  d2,
  input  a1,
  input  b1,
  input  c1,
  input  d1,
  input  a0,
  input  b0,
  input  c0,
  input  d0,
  input  in_17,
  input  in_18,
  output x3,
  output x2,
  output x1,
  output x0
);

  _4_1_Multiplexer u_4_1_multiplexer_1 (.i0(a3), .i1(b3), .i2(c3), .i3(d3), .s1(in_17), .s0(in_18), .out_7(x3));
  _4_1_Multiplexer u_4_1_multiplexer_2 (.i0(a2), .i1(b2), .i2(c2), .i3(d2), .s1(in_17), .s0(in_18), .out_7(x2));
  _4_1_Multiplexer u_4_1_multiplexer_3 (.i0(a1), .i1(b1), .i2(c1), .i3(d1), .s1(in_17), .s0(in_18), .out_7(x1));
  _4_1_Multiplexer u_4_1_multiplexer_4 (.i0(a0), .i1(b0), .i2(c0), .i3(d0), .s1(in_17), .s0(in_18), .out_7(x0));
endmodule

module _4_1_Multiplexer (
  input  i0,
  input  i1,
  input  i2,
  input  i3,
  input  s1,
  input  s0,
  output out_7
);

  wire and_1_out, and_2_out, and_3_out, and_4_out, not_1_out, not_2_out;

  not not_1 (not_1_out, s1);
  not not_2 (not_2_out, s0);
  and and_1 (and_1_out, i0, not_1_out, not_2_out);
  and and_2 (and_2_out, i1, not_1_out, s0);
  and and_3 (and_3_out, i2, s1, not_2_out);
  and and_4 (and_4_out, i3, s1, s0);
  or or_1 (out_7, and_1_out, and_2_out, and_3_out, and_4_out);
endmodule
