// Logisim project p8.circ as structural Verilog: 1 circuit, main circuit main
module main (
  input  i8,
  input  i9,
  input  i10,
  input  i11,
  input  i12,
  input  i13,
  input  i14,
  input  i15,
  input  s4,
  input  s2,
  input  s1,
  input  s0,
  input  i0,
  input  i1,
  input  i2,
  input  i3,
  input  i4,
  input  i5,
  input  i6,
  input  i7,
  input  s4_2,
  input  in_22,
  input  s1_2,
  input  s0_2,
  output x
);

  wire and_1_out, and_2_out, and_3_out, and_4_out, and_5_out, and_6_out, and_7_out, and_8_out, and_9_out,
       and_10_out, and_11_out, and_12_out, and_13_out, and_14_out, and_15_out, and_16_out, not_1_out,
       not_2_out, not_3_out, not_4_out, not_5_out, not_6_out, not_7_out;

  not not_1 (not_1_out, s2);
  not not_2 (not_2_out, s4);
  not not_3 (not_3_out, in_22);
  not not_4 (not_4_out, s1);
  not not_5 (not_5_out, s1_2);
  not not_6 (not_6_out, s0);
  not not_7 (not_7_out, s0_2);
  and and_1 (and_1_out, i8, not_1_out, not_2_out, not_4_out, not_6_out);
  and and_2 (and_2_out, i9, not_1_out, not_2_out, not_4_out, s0);
  and and_3 (and_3_out, i10, not_1_out, not_2_out, s1, not_6_out);
  and and_4 (and_4_out, i11, not_1_out, not_2_out, s1, s0);
  and and_5 (and_5_out, i12, s2, not_2_out, not_4_out, not_6_out);
  and and_6 (and_6_out, i13, s2, not_2_out, not_4_out, s0);
  and and_7 (and_7_out, i14, s2, not_2_out, s1, not_6_out);
  and and_8 (and_8_out, i15, s2, not_2_out, s1, s0);
  and and_9 (and_9_out, i0, not_3_out, s4_2, not_5_out, not_7_out);
  and and_10 (and_10_out, i1, not_3_out, s4_2, not_5_out, s0_2);
  and and_11 (and_11_out, i2, not_3_out, s4_2, s1_2, not_7_out);
  and and_12 (and_12_out, i3, not_3_out, s4_2, s1_2, s0_2);
  and and_13 (and_13_out, i4, in_22, s4_2, not_5_out, not_7_out);
  and and_14 (and_14_out, i5, in_22, s4_2, not_5_out, s0_2);
  and and_15 (and_15_out, i6, in_22, s4_2, s1_2, not_7_out);
  and and_16 (and_16_out, i7, in_22, s4_2, s1_2, s0_2);
  or or_1 (x, and_1_out, and_2_out, and_3_out, and_4_out, and_5_out, and_6_out, and_7_out, and_8_out, and_9_out, and_10_out, and_11_out, and_12_out, and_13_out, and_14_out, and_15_out, and_16_out);
endmodule
