// Logisim project p9.circ as structural Verilog: 3 circuits, main circuit main
module main (
  input  a0,
  input  b0,
  input  a1,
  input  b1,
  output c0,
  output c1,
  output c2
);

  wire half_adder_1_c;

  Half_Adder half_adder_1 (.A(a0), .B(b0), .S(c0), .C(half_adder_1_c));
  Full_Adder full_adder_1 (.A(half_adder_1_c), .B(a1), .C(b1), .Sum(c1), .Carry(c2));
endmodule

module Half_Adder (
  input  A,
  input  B,
  output S,
  output C
);

  xor xor_1 (S, A, B);
  and and_1 (C, A, B);
endmodule

module Full_Adder (
  input  A,
  input  B,
  input  C,
  output Sum,
  output Carry
);

  wire and_1_out, and_2_out, and_3_out, xor_1_out;

  xor xor_1 (xor_1_out, A, B);
  and and_1 (and_1_out, A, B);
  and and_2 (and_2_out, B, C);
  and and_3 (and_3_out, C, A);
  xor xor_2 (Sum, xor_1_out, C);
  or or_1 (Carry, and_1_out, and_2_out, and_3_out);
endmodule
