// Logisim project ADDER _10BIT.circ as structural Verilog: 3 circuits, main circuit main
module main (
  input  C0,
  input  [9:0] in_2,
  input  [9:0] in_3,
  input  _11_AND_12_BIT,
  output [3:0] out_5,
  output [11:0] out_6,
  output [3:0] out_7,
  output [3:0] out_8
);

  wire n4_bit_adder_1_s4, n4_bit_adder_2_s4;

  _4_BIT_ADDER u_4_bit_adder_1 (
    .C0(C0), .A0(in_2[0]), .B0(in_3[0]), .A1(in_2[1]), .B1(in_3[1]), .A2(in_2[2]), .B2(in_3[2]),
    .A3(in_2[3]), .B3(in_3[3]), .S0(out_5[0]), .S1(out_5[1]), .S2(out_5[2]), .S3(out_5[3]),
    .S4(n4_bit_adder_1_s4));
  _4_BIT_ADDER u_4_bit_adder_2 (
    .C0(n4_bit_adder_1_s4), .A0(in_2[4]), .B0(in_3[4]), .A1(in_2[5]), .B1(in_3[5]), .A2(in_2[6]),
    .B2(in_3[6]), .A3(in_2[7]), .B3(in_3[7]), .S0(out_6[4]), .S1(out_6[5]), .S2(out_6[6]), .S3(out_6[7]),
    .S4(n4_bit_adder_2_s4));
  _4_BIT_ADDER u_4_bit_adder_3 (
    .C0(n4_bit_adder_2_s4), .A0(in_2[8]), .B0(in_3[8]), .A1(in_2[9]), .B1(in_3[9]), .A2(_11_AND_12_BIT),
    .B2(_11_AND_12_BIT), .A3(_11_AND_12_BIT), .B3(_11_AND_12_BIT), .S0(out_6[8]), .S1(out_6[9]),
    .S2(out_6[10]), .S3(out_6[11]));  // open: S4

  assign out_6[3:0] = out_5;
  assign out_7 = out_6[7:4];
  assign out_8 = out_6[11:8];
endmodule

module _4_BIT_ADDER (
  input  C0,
  input  A0,
  input  B0,
  input  A1,
  input  B1,
  input  A2,
  input  B2,
  input  A3,
  input  B3,
  output S0,
  output S1,
  output S2,
  output S3,
  output S4
);

  wire full_adder_1_carry, full_adder_2_carry, full_adder_3_carry;

  FULL_ADDER full_adder_1 (.A(C0), .B(A0), .C(B0), .SUM(S0), .CARRY(full_adder_1_carry));
  FULL_ADDER full_adder_2 (.A(full_adder_1_carry), .B(A1), .C(B1), .SUM(S1), .CARRY(full_adder_2_carry));
  FULL_ADDER full_adder_3 (.A(full_adder_2_carry), .B(A2), .C(B2), .SUM(S2), .CARRY(full_adder_3_carry));
  FULL_ADDER full_adder_4 (.A(full_adder_3_carry), .B(A3), .C(B3), .SUM(S3), .CARRY(S4));
endmodule

module FULL_ADDER (
  input  A,
  input  B,
  input  C,
  output SUM,
  output CARRY
);

  wire and_1_out, and_2_out, xor_1_out;

  xor xor_1 (xor_1_out, A, B);
  and and_1 (and_1_out, B, A);
  xor xor_2 (SUM, xor_1_out, C);
  and and_2 (and_2_out, C, xor_1_out);
  or or_1 (CARRY, and_2_out, and_1_out);
endmodule
