// Logisim project ALU16.circ as structural Verilog: 1 circuit, main circuit main
module main (
  input  [15:0] in_1,
  input  [15:0] in_2,
  input  [15:0] in_3,
  input  in_4,
  input  [3:0] in_5,
  output out_6,
  output [15:0] out_7,
  output [15:0] out_8
);

  wire and_2_out, comparator_1_lt, not_4_out, not_5_out;
  wire [15:0] adder_1_out, and_1_out, bit_extender_1_out, C16, divider_1_out, multiplier_1_out, not_1_out,
       not_2_out, not_3_out, or_1_out, REM, subtractor_1_out, xor_1_out;

  Adder #(.width(16)) adder_1 (.a(in_1), .b(in_2), .out(adder_1_out), .cin(in_4));  // open: cout
  Subtractor #(.width(16)) subtractor_1 (.a(in_1), .b(in_2), .out(subtractor_1_out), .bin(in_4));  // open: bout
  Multiplier #(.width(16)) multiplier_1 (.a(in_1), .b(in_2), .out(multiplier_1_out), .cin(in_3), .cout(C16));
  Divider #(.width(16)) divider_1 (.a(in_1), .b(in_2), .out(divider_1_out), .upper(in_3), .rem(REM));
  assign and_1_out = in_1 & in_2;  // AND_Gate and_1, 16 bits wide
  assign or_1_out = in_1 | in_2;  // OR_Gate or_1, 16 bits wide
  Comparator #(.width(16)) comparator_1 (.a(in_1), .b(in_2), .lt(comparator_1_lt));  // open: gt, eq
  assign xor_1_out = in_1 ^ in_2;  // XOR_Gate xor_1, 16 bits wide
  assign not_1_out = ~and_1_out;  // NOT_Gate not_1, 16 bits wide
  assign not_2_out = ~or_1_out;  // NOT_Gate not_2, 16 bits wide
  assign not_3_out = ~xor_1_out;  // NOT_Gate not_3, 16 bits wide
  assign bit_extender_1_out = {{15{1'b0}}, comparator_1_lt};  // Bit_Extender bit_extender_1
  Multiplexer #(.select(4), .width(16)) multiplexer_1 (
    .in0(adder_1_out), .in1(subtractor_1_out), .in2(multiplier_1_out), .in3(divider_1_out), .in4(and_1_out),
    .in5(not_1_out), .in6(or_1_out), .in7(not_2_out), .in8(xor_1_out), .in9(not_3_out),
    .in10(bit_extender_1_out), .in11(in_3), .in12(in_3), .in13(in_3), .in14(in_3), .in15(in_3), .out(out_7),
    .sel(in_5));  // open: en
  Comparator #(.width(16)) comparator_2 (.a(in_3), .b(out_7), .eq(out_6));  // open: gt, lt
  not not_4 (not_4_out, in_5[2]);
  not not_5 (not_5_out, in_5[2]);
  and and_2 (and_2_out, not_4_out, not_5_out, in_5[1]);
  Multiplexer #(.width(16)) multiplexer_2 (.in0(C16), .in1(REM), .out(out_8), .sel(in_5[0]), .en(and_2_out));

  // Other names for the same wires on the sheet: A[15:0] = in_1; B[15:0] = in_2; C0[15:0] = in_3; s0 = in_5[0];
  //   s1 = in_5[1]; s2 = in_5[2]; s3 = in_5[3]
endmodule
