// Logisim project ALU4.circ as structural Verilog: 5 circuits, main circuit main
module main (
  input  A0,
  input  B0,
  input  A1,
  input  B1,
  input  A2,
  input  B2,
  input  A3,
  input  B3,
  input  [1:0] in_9,
  output [3:0] out_10
);

  wire [3:0] bitwise_and_1_s0, bitwise_or_1_s0, n4_bit_adder_1_s0;

  _4_BIT_ADDER u_4_bit_adder_1 (
    .CONTROL(in_9[0]), .A0(A0), .B0(B0), .A1(A1), .B1(B1), .A2(A2), .B2(B2), .A3(A3), .B3(B3),
    .S0(n4_bit_adder_1_s0[0]), .S1(n4_bit_adder_1_s0[1]), .S2(n4_bit_adder_1_s0[2]), .S3(n4_bit_adder_1_s0[3]));  // open: OVERFLOW
  BITWISE_AND bitwise_and_1 (
    .A0(A0), .B0(B0), .A1(A1), .B1(B1), .A2(A2), .B2(B2), .A3(A3), .B3(B3), .S0(bitwise_and_1_s0[0]),
    .S1(bitwise_and_1_s0[1]), .S2(bitwise_and_1_s0[2]), .S3(bitwise_and_1_s0[3]));
  BITWISE_OR bitwise_or_1 (
    .A0(A0), .B0(B0), .A1(A1), .B1(B1), .A2(A2), .B2(B2), .A3(A3), .B3(B3), .S0(bitwise_or_1_s0[0]),
    .S1(bitwise_or_1_s0[1]), .S2(bitwise_or_1_s0[2]), .S3(bitwise_or_1_s0[3]));
  Multiplexer #(.select(2), .width(4)) multiplexer_1 (
    .in0(n4_bit_adder_1_s0), .in1(n4_bit_adder_1_s0), .in2(bitwise_and_1_s0), .in3(bitwise_or_1_s0),
    .out(out_10), .sel(in_9));  // open: en

  // Other names for the same wires on the sheet: S0 = in_9[0]; S1 = in_9[1]
endmodule

module FULL_ADDER (
  input  A,
  input  B,
  input  C,
  output SUM,
  output CARRY
);

  wire and_1_out, and_2_out, xor_1_out;

  xor xor_1 (xor_1_out, A, B);
  and and_1 (and_1_out, B, A);
  xor xor_2 (SUM, xor_1_out, C);
  and and_2 (and_2_out, C, xor_1_out);
  or or_1 (CARRY, and_2_out, and_1_out);
endmodule

module _4_BIT_ADDER (
  input  CONTROL,
  input  A0,
  input  B0,
  input  A1,
  input  B1,
  input  A2,
  input  B2,
  input  A3,
  input  B3,
  output S0,
  output S1,
  output S2,
  output S3,
  output OVERFLOW
);

  wire full_adder_1_carry, full_adder_2_carry, full_adder_3_carry, xor_1_out, xor_2_out, xor_3_out, xor_4_out;

  xor xor_1 (xor_1_out, CONTROL, B0);
  xor xor_2 (xor_2_out, CONTROL, B1);
  xor xor_3 (xor_3_out, CONTROL, B2);
  xor xor_4 (xor_4_out, CONTROL, B3);
  FULL_ADDER full_adder_1 (.A(CONTROL), .B(A0), .C(xor_1_out), .SUM(S0), .CARRY(full_adder_1_carry));
  FULL_ADDER full_adder_2 (.A(full_adder_1_carry), .B(A1), .C(xor_2_out), .SUM(S1), .CARRY(full_adder_2_carry));
  FULL_ADDER full_adder_3 (.A(full_adder_2_carry), .B(A2), .C(xor_3_out), .SUM(S2), .CARRY(full_adder_3_carry));
  FULL_ADDER full_adder_4 (.A(full_adder_3_carry), .B(A3), .C(xor_4_out), .SUM(S3), .CARRY(OVERFLOW));
endmodule

module BITWISE_AND (
  input  A0,
  input  B0,
  input  A1,
  input  B1,
  input  A2,
  input  B2,
  input  A3,
  input  B3,
  output S0,
  output S1,
  output S2,
  output S3
);

  and and_1 (S0, A0, B0);
  and and_2 (S1, A1, B1);
  and and_3 (S2, A2, B2);
  and and_4 (S3, A3, B3);
endmodule

module BITWISE_OR (
  input  A0,
  input  B0,
  input  A1,
  input  B1,
  input  A2,
  input  B2,
  input  A3,
  input  B3,
  output S0,
  output S1,
  output S2,
  output S3
);

  or or_1 (S0, A0, B0);
  or or_2 (S1, A1, B1);
  or or_3 (S2, A2, B2);
  or or_4 (S3, A3, B3);
endmodule
