// Logisim project P0.circ as structural Verilog: 1 circuit, main circuit main
module main (
  input  A,
  input  C,
  input  B,
  input  D,
  input  E,
  input  F,
  input  Preset,
  input  PRESET2,
  input  PRESET3,
  input  PRESET4,
  input  Enable,
  input  ENABLE2,
  input  ENABLE3,
  input  ENABLE4,
  input  CLEAR3,
  input  CLEAR4,
  input  CLEAR2,
  input  Clear,
  output Q1,
  output Q2,
  output Q3,
  output Q4
);

  wire clock_1_out, clock_2_out, clock_3_out, clock_4_out;

  Clock clock_1 (.out(clock_1_out));
  J_K_Flip_Flop j_k_ff_1 (
    .J(A), .clk(clock_1_out), .K(B), .Q(Q1), .preset(Preset), .en(Enable), .reset(Clear));  // open: Qn
  Clock clock_2 (.out(clock_2_out));
  S_R_Flip_Flop s_r_ff_1 (
    .S(C), .clk(clock_2_out), .R(D), .Q(Q2), .preset(PRESET2), .reset(CLEAR2), .en(ENABLE2));  // open: Qn
  Clock clock_3 (.out(clock_3_out));
  D_Flip_Flop d_ff_1 (.clk(clock_3_out), .D(E), .Q(Q3), .preset(PRESET3), .en(ENABLE3), .reset(CLEAR3));  // open: Qn
  Clock clock_4 (.out(clock_4_out));
  T_Flip_Flop t_ff_1 (.clk(clock_4_out), .T(F), .Q(Q4), .preset(PRESET4), .reset(CLEAR4), .en(ENABLE4));  // open: Qn

  // Notes on the sheet:
  //   JK FLIPFLOP
  //   SR FLIPFLOP
  //   D FLIPFLOP
  //   T FLIPFLOP
endmodule
