// Logisim project P2.circ as structural Verilog: 1 circuit, main circuit main
module main (
  input  _0_OR_1,
  output [3:0] OUT
);

  wire clock_1_out;
  wire [3:0] RAN_out;

  Clock clock_1 (.out(clock_1_out));
  Random #(.width(4)) RAN (.clk(clock_1_out), .out(RAN_out));  // open: next, clr
  Hex_Digit_Display hex_digit_display_1 (.value(RAN_out));  // open: dp
  Hex_Digit_Display hex_digit_display_2 (.value(OUT));  // open: dp
  D_Flip_Flop d_ff_1 (.clk(clock_1_out), .D(RAN_out[0]), .Q(OUT[0]), .en(_0_OR_1));  // open: Qn, preset, reset
  D_Flip_Flop d_ff_2 (.clk(clock_1_out), .D(RAN_out[1]), .Q(OUT[1]), .en(_0_OR_1));  // open: Qn, preset, reset
  D_Flip_Flop d_ff_3 (.clk(clock_1_out), .D(RAN_out[2]), .Q(OUT[2]), .en(_0_OR_1));  // open: Qn, preset, reset
  D_Flip_Flop d_ff_4 (.clk(clock_1_out), .D(RAN_out[3]), .Q(OUT[3]), .en(_0_OR_1));  // open: Qn, preset, reset
endmodule
