// Logisim project P3.circ as structural Verilog: 1 circuit, main circuit main
module main (
  input  IN,
  input  in_2,
  output S0,
  output S1,
  output S2,
  output S3,
  output S4,
  output S5
);

  wire clock_1_out;

  Hex_Digit_Display hex_digit_display_1 (.value({2'b00, S5, S4}));  // open: dp
  Clock clock_1 (.out(clock_1_out));
  Hex_Digit_Display hex_digit_display_2 (.value({S3, S2, S1, S0}));  // open: dp
  T_Flip_Flop t_ff_1 (.clk(clock_1_out), .T(IN), .Q(S0), .reset(in_2));  // open: Qn, preset, en
  T_Flip_Flop t_ff_2 (.clk(S0), .T(IN), .Q(S1), .reset(in_2));  // open: Qn, preset, en
  T_Flip_Flop t_ff_3 (.clk(S1), .T(IN), .Q(S2), .reset(in_2));  // open: Qn, preset, en
  T_Flip_Flop t_ff_4 (.clk(S2), .T(IN), .Q(S3), .reset(in_2));  // open: Qn, preset, en
  T_Flip_Flop t_ff_5 (.clk(S3), .T(IN), .Q(S4), .reset(in_2));  // open: Qn, preset, en
  T_Flip_Flop t_ff_6 (.clk(S4), .T(IN), .Q(S5), .reset(in_2));  // open: Qn, preset, en
endmodule
