// Logisim project L9Q1_D.circ as structural Verilog: 1 circuit, main circuit main
module main (
  output QA,
  output QB,
  output QC,
  output QD
);

  wire and_1_out, and_2_out, clock_1_out, DA_qn, xor_1_out, xor_2_out, xor_3_out;

  Clock clock_1 (.out(clock_1_out));
  D_Flip_Flop DA (.clk(clock_1_out), .D(DA_qn), .Q(QA), .Qn(DA_qn));  // open: preset, en, reset
  xor xor_1 (xor_1_out, QA, QB);
  and and_1 (and_1_out, QA, QB);
  D_Flip_Flop DB (.clk(clock_1_out), .D(xor_1_out), .Q(QB));  // open: Qn, preset, en, reset
  xor xor_2 (xor_2_out, and_1_out, QC);
  and and_2 (and_2_out, and_1_out, QC);
  D_Flip_Flop DC (.clk(clock_1_out), .D(xor_2_out), .Q(QC));  // open: Qn, preset, en, reset
  xor xor_3 (xor_3_out, and_2_out, QD);
  D_Flip_Flop DD (.clk(clock_1_out), .D(xor_3_out), .Q(QD));  // open: Qn, preset, en, reset
endmodule
