// Logisim project L9Q1_JK.circ as structural Verilog: 1 circuit, main circuit main
module main (
  output QA,
  output QB,
  output QC,
  output QD
);

  wire and_1_out, and_2_out, clock_1_out;

  Clock clock_1 (.out(clock_1_out));
  J_K_Flip_Flop JKA (.J(1'b1), .clk(clock_1_out), .K(1'b1), .Q(QA));  // open: Qn, preset, en, reset
  J_K_Flip_Flop JKB (.J(QA), .clk(clock_1_out), .K(QA), .Q(QB));  // open: Qn, preset, en, reset
  and and_1 (and_1_out, QB, QA);
  J_K_Flip_Flop JKC (.J(and_1_out), .clk(clock_1_out), .K(and_1_out), .Q(QC));  // open: Qn, preset, en, reset
  and and_2 (and_2_out, and_1_out, QC);
  J_K_Flip_Flop JKD (.J(and_2_out), .clk(clock_1_out), .K(and_2_out), .Q(QD));  // open: Qn, preset, en, reset
endmodule
