// Logisim project L9Q1_SR.circ as structural Verilog: 1 circuit, main circuit main
module main (
  output QC,
  output QD,
  output QA,
  output QB
);

  wire and_1_out, and_2_out, and_3_out, and_4_out, and_5_out, and_6_out, and_7_out, and_8_out, clock_1_out,
       s_r_ff_1_qn, s_r_ff_2_qn, s_r_ff_3_qn, s_r_ff_4_qn;

  Clock clock_1 (.out(clock_1_out));
  S_R_Flip_Flop s_r_ff_1 (
    .S(s_r_ff_1_qn), .clk(clock_1_out), .R(QA), .Q(QA), .Qn(s_r_ff_1_qn));  // open: preset, reset, en
  and and_1 (and_1_out, s_r_ff_2_qn, QA);
  and and_2 (and_2_out, QA, QB);
  and and_3 (and_3_out, QA, QB);
  S_R_Flip_Flop s_r_ff_2 (
    .S(and_1_out), .clk(clock_1_out), .R(and_2_out), .Q(QB), .Qn(s_r_ff_2_qn));  // open: preset, reset, en
  and and_4 (and_4_out, s_r_ff_3_qn, and_3_out);
  and and_5 (and_5_out, and_3_out, QC);
  S_R_Flip_Flop s_r_ff_3 (
    .S(and_4_out), .clk(clock_1_out), .R(and_5_out), .Q(QC), .Qn(s_r_ff_3_qn));  // open: preset, reset, en
  and and_6 (and_6_out, and_3_out, QC);
  and and_7 (and_7_out, and_6_out, s_r_ff_4_qn);
  and and_8 (and_8_out, and_6_out, QD);
  S_R_Flip_Flop s_r_ff_4 (
    .S(and_7_out), .clk(clock_1_out), .R(and_8_out), .Q(QD), .Qn(s_r_ff_4_qn));  // open: preset, reset, en
endmodule
