// Logisim project L9Q1_T.circ as structural Verilog: 1 circuit, main circuit main
module main (
  output QA,
  output QB,
  output QC,
  output QD
);

  wire and_1_out, and_2_out, clock_1_out;

  Clock clock_1 (.out(clock_1_out));
  T_Flip_Flop TA (.clk(clock_1_out), .T(1'b1), .Q(QA));  // open: Qn, preset, reset, en
  T_Flip_Flop TB (.clk(clock_1_out), .T(QA), .Q(QB));  // open: Qn, preset, reset, en
  and and_1 (and_1_out, QB, QA);
  T_Flip_Flop TC (.clk(clock_1_out), .T(and_1_out), .Q(QC));  // open: Qn, preset, reset, en
  and and_2 (and_2_out, and_1_out, QC);
  T_Flip_Flop TD (.clk(clock_1_out), .T(and_2_out), .Q(QD));  // open: Qn, preset, reset, en
endmodule
