// Logisim project L9Q3.circ as structural Verilog: 3 circuits, main circuit main
module main (
  input  [3:0] WRITER,
  input  [3:0] READ0,
  input  [3:0] READ1,
  input  [15:0] C0,
  input  REGWRITE,
  input  REGCLEAR,
  input  [15:0] WRITE_VALUE,
  input  [3:0] SELECTOR,
  output out_9,
  output [15:0] VALUE1,
  output [15:0] RESULT,
  output [15:0] VALUE0,
  output [15:0] _16BITCARRY
);

  wire CLOCK_out;

  Clock CLOCK (.out(CLOCK_out));
  REGISTER16IT register16it_1 (
    .WRITER(WRITER), .WRITE_VALUE(WRITE_VALUE), .CLOCK(CLOCK_out), .REGWRITE(REGWRITE), .REGCLEAR(REGCLEAR),
    .READ1(READ1), .READ0(READ0), .VALUE1(VALUE1), .VALUE0(VALUE0));
  ALU16 alu16_1 (
    .A(VALUE1), .B(VALUE0), .C0(C0), .SELECTOR(SELECTOR), .out_6(out_9), .OUTPUT(RESULT),
    ._16BITCARRY(_16BITCARRY));  // open: in_4
endmodule

module REGISTER16IT (
  input  [3:0] READ1,
  input  [3:0] WRITER,
  input  [15:0] WRITE_VALUE,
  input  [3:0] READ0,
  input  REGWRITE,
  input  CLOCK,
  input  REGCLEAR,
  output [15:0] VALUE1,
  output [15:0] VALUE0
);

  wire and_1_out, and_2_out, and_3_out, and_4_out, and_5_out, and_6_out, and_7_out, and_8_out, and_9_out,
       and_10_out, and_11_out, and_12_out, and_13_out, and_14_out, and_15_out, and_16_out, decoder_1_out0,
       decoder_1_out1, decoder_1_out2, decoder_1_out3, decoder_1_out4, decoder_1_out5, decoder_1_out6,
       decoder_1_out7, decoder_1_out8, decoder_1_out9, decoder_1_out10, decoder_1_out11, decoder_1_out12,
       decoder_1_out13, decoder_1_out14, decoder_1_out15;
  wire [15:0] register_1_q, register_2_q, register_3_q, register_4_q, register_5_q, register_6_q,
       register_7_q, register_8_q, register_9_q, register_10_q, register_11_q, register_12_q, register_13_q,
       register_14_q, register_15_q, register_16_q;

  Decoder #(.select(4)) decoder_1 (
    .out0(decoder_1_out0), .out1(decoder_1_out1), .out2(decoder_1_out2), .out3(decoder_1_out3),
    .out4(decoder_1_out4), .out5(decoder_1_out5), .out6(decoder_1_out6), .out7(decoder_1_out7),
    .out8(decoder_1_out8), .out9(decoder_1_out9), .out10(decoder_1_out10), .out11(decoder_1_out11),
    .out12(decoder_1_out12), .out13(decoder_1_out13), .out14(decoder_1_out14), .out15(decoder_1_out15),
    .sel(WRITER));  // open: en
  and and_1 (and_1_out, REGWRITE, decoder_1_out0);
  and and_2 (and_2_out, REGWRITE, decoder_1_out1);
  and and_3 (and_3_out, REGWRITE, decoder_1_out2);
  and and_4 (and_4_out, REGWRITE, decoder_1_out3);
  and and_5 (and_5_out, REGWRITE, decoder_1_out4);
  and and_6 (and_6_out, REGWRITE, decoder_1_out5);
  and and_7 (and_7_out, REGWRITE, decoder_1_out6);
  and and_8 (and_8_out, REGWRITE, decoder_1_out7);
  and and_9 (and_9_out, REGWRITE, decoder_1_out8);
  and and_10 (and_10_out, REGWRITE, decoder_1_out9);
  and and_11 (and_11_out, REGWRITE, decoder_1_out10);
  and and_12 (and_12_out, REGWRITE, decoder_1_out11);
  and and_13 (and_13_out, REGWRITE, decoder_1_out12);
  and and_14 (and_14_out, REGWRITE, decoder_1_out13);
  and and_15 (and_15_out, REGWRITE, decoder_1_out14);
  and and_16 (and_16_out, REGWRITE, decoder_1_out15);
  Register #(.width(16)) register_1 (.D(WRITE_VALUE), .en(and_1_out), .Q(register_1_q), .clk(CLOCK), .clr(REGCLEAR));
  Register #(.width(16)) register_2 (.D(WRITE_VALUE), .en(and_2_out), .Q(register_2_q), .clk(CLOCK), .clr(REGCLEAR));
  Register #(.width(16)) register_3 (.D(WRITE_VALUE), .en(and_3_out), .Q(register_3_q), .clk(CLOCK), .clr(REGCLEAR));
  Register #(.width(16)) register_4 (.D(WRITE_VALUE), .en(and_4_out), .Q(register_4_q), .clk(CLOCK), .clr(REGCLEAR));
  Register #(.width(16)) register_5 (.D(WRITE_VALUE), .en(and_5_out), .Q(register_5_q), .clk(CLOCK), .clr(REGCLEAR));
  Register #(.width(16)) register_6 (.D(WRITE_VALUE), .en(and_6_out), .Q(register_6_q), .clk(CLOCK), .clr(REGCLEAR));
  Register #(.width(16)) register_7 (.D(WRITE_VALUE), .en(and_7_out), .Q(register_7_q), .clk(CLOCK), .clr(REGCLEAR));
  Register #(.width(16)) register_8 (.D(WRITE_VALUE), .en(and_8_out), .Q(register_8_q), .clk(CLOCK), .clr(REGCLEAR));
  Register #(.width(16)) register_9 (.D(WRITE_VALUE), .en(and_9_out), .Q(register_9_q), .clk(CLOCK), .clr(REGCLEAR));
  Register #(.width(16)) register_10 (.D(WRITE_VALUE), .en(and_10_out), .Q(register_10_q), .clk(CLOCK), .clr(REGCLEAR));
  Register #(.width(16)) register_11 (.D(WRITE_VALUE), .en(and_11_out), .Q(register_11_q), .clk(CLOCK), .clr(REGCLEAR));
  Register #(.width(16)) register_12 (.D(WRITE_VALUE), .en(and_12_out), .Q(register_12_q), .clk(CLOCK), .clr(REGCLEAR));
  Register #(.width(16)) register_13 (.D(WRITE_VALUE), .en(and_13_out), .Q(register_13_q), .clk(CLOCK), .clr(REGCLEAR));
  Register #(.width(16)) register_14 (.D(WRITE_VALUE), .en(and_14_out), .Q(register_14_q), .clk(CLOCK), .clr(REGCLEAR));
  Register #(.width(16)) register_15 (.D(WRITE_VALUE), .en(and_15_out), .Q(register_15_q), .clk(CLOCK), .clr(REGCLEAR));
  Register #(.width(16)) register_16 (.D(WRITE_VALUE), .en(and_16_out), .Q(register_16_q), .clk(CLOCK), .clr(REGCLEAR));
  Multiplexer #(.select(4), .width(16)) multiplexer_1 (
    .in0(register_1_q), .in1(register_2_q), .in2(register_3_q), .in3(register_4_q), .in4(register_5_q),
    .in5(register_6_q), .in6(register_7_q), .in7(register_8_q), .in8(register_9_q), .in9(register_10_q),
    .in10(register_11_q), .in11(register_12_q), .in12(register_13_q), .in13(register_14_q),
    .in14(register_15_q), .in15(register_16_q), .out(VALUE1), .sel(READ1));  // open: en
  Multiplexer #(.select(4), .width(16)) multiplexer_2 (
    .in0(register_1_q), .in1(register_2_q), .in2(register_3_q), .in3(register_4_q), .in4(register_5_q),
    .in5(register_6_q), .in6(register_7_q), .in7(register_8_q), .in8(register_9_q), .in9(register_10_q),
    .in10(register_11_q), .in11(register_12_q), .in12(register_13_q), .in13(register_14_q),
    .in14(register_15_q), .in15(register_16_q), .out(VALUE0), .sel(READ0));  // open: en
endmodule

module ALU16 (
  input  [15:0] A,
  input  [15:0] B,
  input  [15:0] C0,
  input  in_4,
  input  [3:0] SELECTOR,
  output out_6,
  output [15:0] OUTPUT,
  output [15:0] _16BITCARRY
);

  wire and_2_out, comparator_1_lt, not_4_out, not_5_out;
  wire [15:0] adder_1_out, and_1_out, bit_extender_1_out, C16, divider_1_out, multiplier_1_out, not_1_out,
       not_2_out, not_3_out, or_1_out, REM, subtractor_1_out, xor_1_out;

  Adder #(.width(16)) adder_1 (.a(A), .b(B), .out(adder_1_out), .cin(in_4));  // open: cout
  Subtractor #(.width(16)) subtractor_1 (.a(A), .b(B), .out(subtractor_1_out), .bin(in_4));  // open: bout
  Multiplier #(.width(16)) multiplier_1 (.a(A), .b(B), .out(multiplier_1_out), .cin(C0), .cout(C16));
  Divider #(.width(16)) divider_1 (.a(A), .b(B), .out(divider_1_out), .upper(C0), .rem(REM));
  assign and_1_out = A & B;  // AND_Gate and_1, 16 bits wide
  assign or_1_out = A | B;  // OR_Gate or_1, 16 bits wide
  Comparator #(.width(16)) comparator_1 (.a(A), .b(B), .lt(comparator_1_lt));  // open: gt, eq
  assign xor_1_out = A ^ B;  // XOR_Gate xor_1, 16 bits wide
  assign not_1_out = ~and_1_out;  // NOT_Gate not_1, 16 bits wide
  assign not_2_out = ~or_1_out;  // NOT_Gate not_2, 16 bits wide
  assign not_3_out = ~xor_1_out;  // NOT_Gate not_3, 16 bits wide
  assign bit_extender_1_out = {{15{1'b0}}, comparator_1_lt};  // Bit_Extender bit_extender_1
  Multiplexer #(.select(4), .width(16)) multiplexer_1 (
    .in0(adder_1_out), .in1(subtractor_1_out), .in2(multiplier_1_out), .in3(divider_1_out), .in4(and_1_out),
    .in5(not_1_out), .in6(or_1_out), .in7(not_2_out), .in8(xor_1_out), .in9(not_3_out),
    .in10(bit_extender_1_out), .in11(C0), .in12(C0), .in13(C0), .in14(C0), .in15(C0), .out(OUTPUT),
    .sel(SELECTOR));  // open: en
  Comparator #(.width(16)) comparator_2 (.a(C0), .b(OUTPUT), .eq(out_6));  // open: gt, lt
  not not_4 (not_4_out, SELECTOR[2]);
  not not_5 (not_5_out, SELECTOR[2]);
  and and_2 (and_2_out, not_4_out, not_5_out, SELECTOR[1]);
  Multiplexer #(.width(16)) multiplexer_2 (.in0(C16), .in1(REM), .out(_16BITCARRY), .sel(SELECTOR[0]), .en(and_2_out));

  // Other names for the same wires on the sheet: s0 = SELECTOR[0]; s1 = SELECTOR[1]; s2 = SELECTOR[2];
  //   s3 = SELECTOR[3]
endmodule
