// Logisim project CS226 PROJECT IMPLEMENTATION.circ as structural Verilog: 3 circuits, main circuit main
module main (
  output X,
  output QB,
  output QA,
  output Y,
  output OUT,
  output Z,
  output TA,
  output TB
);

  wire and_1_out, and_2_out, and_3_out, and_4_out, and_5_out, and_6_out, and_7_out, clock_1_out, d_ff_1_q,
       not_1_out, not_2_out, not_3_out, not_4_out, not_5_out, or_2_out, random_generator_1_1_output_y,
       random_generator_1_2_output_y;
  wire [3:0] n4_bit_up_counter_1_out_3;

  Clock clock_1 (.out(clock_1_out));
  D_Flip_Flop d_ff_1 (.clk(clock_1_out), .D(OUT), .Q(d_ff_1_q));  // open: Qn, preset, en, reset
  Hex_Digit_Display hex_digit_display_1 (.value(n4_bit_up_counter_1_out_3));  // open: dp
  _4_BIT_UP_Counter u_4_bit_up_counter_1 (
    .CLOCK(clock_1_out), .RESET(d_ff_1_q), .out_3(n4_bit_up_counter_1_out_3), .OUT_X(X), .OUT_MID(Y));
  RANDOM_GENERATOR_1 random_generator_1_1 (.CLOCK(clock_1_out), .OUTPUT_Y(random_generator_1_1_output_y));
  RANDOM_GENERATOR_1 random_generator_1_2 (.CLOCK(clock_1_out), .OUTPUT_Y(random_generator_1_2_output_y));
  Multiplexer multiplexer_1 (
    .in0(random_generator_1_1_output_y), .in1(random_generator_1_2_output_y), .out(Z), .sel(QA));  // open: en
  T_Flip_Flop t_ff_1 (.clk(clock_1_out), .T(TB), .Q(QB));  // open: Qn, preset, reset, en
  not not_1 (not_1_out, QA);
  not not_2 (not_2_out, QB);
  and and_1 (and_1_out, Y, QB);
  and and_2 (and_2_out, Z, QB);
  LED led_1 (.in(not_1_out));
  and and_3 (and_3_out, QA, not_2_out);
  and and_4 (and_4_out, QB, QA);
  or or_1 (TA, Z, and_1_out);
  LED led_2 (.in(and_4_out));
  LED led_3 (.in(and_3_out));
  T_Flip_Flop t_ff_2 (.clk(clock_1_out), .T(TA), .Q(QA));  // open: Qn, preset, reset, en
  or or_2 (or_2_out, and_1_out, and_2_out);
  or or_3 (OUT, X, TA);
  not not_3 (not_3_out, QA);
  not not_4 (not_4_out, QB);
  not not_5 (not_5_out, Z);
  and and_5 (and_5_out, not_3_out, QB);
  and and_6 (and_6_out, not_3_out, not_4_out);
  and and_7 (and_7_out, X, not_5_out);
  or or_4 (TB, and_7_out, or_2_out);
  LED led_4 (.in(QA));
  LED led_5 (.in(and_5_out));
  LED led_6 (.in(and_6_out));
endmodule

module RANDOM_GENERATOR_1 (
  input  CLOCK,
  output OUTPUT_Y
);

  wire and_1_out, and_2_out, and_3_out, not_1_out, or_1_out, or_2_out, random_1_out, S0, S1;

  Random #(.width(1)) random_1 (.clk(CLOCK), .out(random_1_out));  // open: next, clr
  not not_1 (not_1_out, random_1_out);
  or or_1 (or_1_out, not_1_out, S0);
  T_Flip_Flop t_ff_1 (.clk(CLOCK), .T(or_1_out), .Q(S0));  // open: Qn, preset, reset, en
  and and_1 (and_1_out, S0, random_1_out);
  and and_2 (and_2_out, random_1_out, S1);
  and and_3 (and_3_out, S1, S0);
  or or_2 (or_2_out, and_1_out, and_2_out, and_3_out);
  T_Flip_Flop t_ff_2 (.clk(CLOCK), .T(or_2_out), .Q(S1));  // open: Qn, preset, reset, en
  and and_4 (OUTPUT_Y, or_1_out, and_3_out);
endmodule

module _4_BIT_UP_Counter (
  input  CLOCK,
  input  RESET,
  output [3:0] out_3,
  output OUT_X,
  output OUT_MID
);

  wire and_2_out;

  T_Flip_Flop t_ff_1 (.clk(CLOCK), .T(1'b1), .Q(out_3[0]), .reset(RESET));  // open: Qn, preset, en
  T_Flip_Flop t_ff_2 (.clk(CLOCK), .T(out_3[0]), .Q(out_3[1]), .reset(RESET));  // open: Qn, preset, en
  T_Flip_Flop t_ff_3 (.clk(CLOCK), .T(OUT_MID), .Q(out_3[2]), .reset(RESET));  // open: Qn, preset, en
  and and_1 (OUT_MID, out_3[1], out_3[0]);
  and and_2 (and_2_out, out_3[2], OUT_MID);
  T_Flip_Flop t_ff_4 (.clk(CLOCK), .T(and_2_out), .Q(out_3[3]), .reset(RESET));  // open: Qn, preset, en
  and and_3 (OUT_X, out_3[3], and_2_out);
endmodule
